// Logisim project IT012-Lab01_3.2.circ as structural Verilog: 1 circuit, main circuit main
module main (
  input  A,
  input  B,
  input  C,
  input  D,
  output A_o,
  output B_o,
  output C_p,
  output D_o
);

  wire clock_out;

  Clock clock (.out(clock_out));
  Register #(.width(4)) register_1 (
    .D({D, C, B, A}), .en(1'b1), .Q({D_o, C_p, B_o, A_o}), .clk(clock_out));  // open: clr
endmodule
