// Logisim project IT012-Lab01_3.2_2.circ as structural Verilog: 1 circuit, main circuit main
module main (
  input  [3:0] A,
  input  [3:0] B,
  input  [3:0] C,
  input  [3:0] D,
  output [3:0] A_o,
  output [3:0] B_o,
  output [3:0] C_p,
  output [3:0] D_o
);

  wire clock_out;

  Clock clock (.out(clock_out));
  Register #(.width(4)) register_1 (.D(A), .Q(A_o), .clk(clock_out));  // open: en, clr
  Register #(.width(4)) register_2 (.D(B), .Q(B_o), .clk(clock_out));  // open: en, clr
  Register #(.width(4)) register_3 (.D(C), .Q(C_p), .clk(clock_out));  // open: en, clr
  Register #(.width(4)) register_4 (.D(D), .Q(D_o), .clk(clock_out));  // open: en, clr
endmodule
