// Logisim project IT012-Lab01_A1.circ as structural Verilog: 1 circuit, main circuit main
module main (
  input  A,
  input  B,
  input  C,
  output x
);

  wire AB_out, ABC_out, AC_out, BC_out;

  and ABC (ABC_out, A, B, C);
  and AB (AB_out, A, B);
  and AC (AC_out, A, C);
  and BC (BC_out, B, C);
  or or_1 (x, ABC_out, AB_out, AC_out, BC_out, C);
endmodule
