// Logisim project ALU mo phong op3.circ as structural Verilog: 1 circuit, main circuit main
module main (
  input  [7:0] A,
  input  [1:0] in_2,
  input  [7:0] B,
  output [7:0] S
);

  wire [7:0] adder_1_out, and_1_out, nand_1_out, subtractor_1_out;

  Adder adder_1 (.a(A), .b(B), .out(adder_1_out));  // open: cin, cout
  Subtractor subtractor_1 (.a(A), .b(B), .out(subtractor_1_out));  // open: bin, bout
  assign and_1_out = A & B;  // AND_Gate and_1, 8 bits wide
  assign nand_1_out = ~(A & B);  // NAND_Gate nand_1, 8 bits wide
  Multiplexer #(.select(2), .width(8), .enable("false")) multiplexer_1 (
    .in0(adder_1_out), .in1(subtractor_1_out), .in2(and_1_out), .in3(nand_1_out), .out(S), .sel(in_2));
endmodule
