// Logisim project adder8but.circ as structural Verilog: 1 circuit, main circuit main
module main (
  input  A0,
  input  A1,
  input  A2,
  input  A0_2,
  input  A1_2,
  input  A2_2,
  input  A1_3,
  input  A2_3,
  input  A0_3,
  input  A1_4,
  input  A2_4,
  input  A0_4,
  input  A1_5,
  input  A2_5,
  input  A1_6,
  input  A2_6,
  output out_17,
  output out_18,
  output out_19,
  output out_20,
  output out_21,
  output out_22,
  output out_23,
  output out_24,
  output out_25
);

  wire adder_1_cout, adder_2_cout, adder_3_cout, adder_4_cout, adder_5_cout, adder_6_cout, adder_7_cout;

  Adder #(.width(1)) adder_1 (.a(A0), .b(A0_3), .out(out_17), .cout(adder_1_cout));  // open: cin
  Adder #(.width(1)) adder_2 (.a(A1), .b(A1_4), .out(out_18), .cin(adder_1_cout), .cout(adder_2_cout));
  Adder #(.width(1)) adder_3 (.a(A2), .b(A2_4), .out(out_19), .cin(adder_2_cout), .cout(adder_3_cout));
  Adder #(.width(1)) adder_4 (.a(A0_2), .b(A0_4), .out(out_20), .cin(adder_3_cout), .cout(adder_4_cout));
  Adder #(.width(1)) adder_5 (.a(A1_2), .b(A1_5), .out(out_21), .cin(adder_4_cout), .cout(adder_5_cout));
  Adder #(.width(1)) adder_6 (.a(A2_2), .b(A2_5), .out(out_22), .cin(adder_5_cout), .cout(adder_6_cout));
  Adder #(.width(1)) adder_7 (.a(A1_3), .b(A1_6), .out(out_23), .cin(adder_6_cout), .cout(adder_7_cout));
  Adder #(.width(1)) adder_8 (.a(A2_3), .b(A2_6), .out(out_24), .cin(adder_7_cout), .cout(out_25));
endmodule
