// Logisim project decode2to4.circ as structural Verilog: 1 circuit, main circuit main
module main (
  input  A,
  input  B,
  output y0,
  output y1,
  output y2,
  output y3
);

  wire not_1_out, not_2_out;

  not not_1 (not_1_out, A);
  not not_2 (not_2_out, B);
  and and_1 (y0, not_2_out, not_1_out);
  and and_2 (y1, B, not_1_out);
  and and_3 (y2, not_2_out, A);
  and and_4 (y3, B, A);
endmodule
