// Logisim project mux4to1.circ as structural Verilog: 1 circuit, main circuit main
module main (
  input  X1,
  input  X2,
  input  X3,
  input  X4,
  input  C2,
  input  C1,
  output Y
);

  wire and_1_out, and_2_out, and_3_out, and_4_out, not_1_out, not_2_out;

  not not_1 (not_1_out, C2);
  not not_2 (not_2_out, C1);
  and and_1 (and_1_out, X1, not_2_out, not_1_out);
  and and_2 (and_2_out, X2, not_2_out, C2);
  and and_3 (and_3_out, X3, C1, not_1_out);
  and and_4 (and_4_out, X4, C1, C2);
  or or_1 (Y, and_1_out, and_2_out, and_3_out, and_4_out);
endmodule
