// Logisim project register files.circ as structural Verilog: 1 circuit, main circuit main
module main (
  input  [7:0] A,
  input  [1:0] B,
  input  C,
  output [7:0] F
);

  wire CLK_out, decoder_1_out0, decoder_1_out1, decoder_1_out2, decoder_1_out3;
  wire [7:0] register_1_q, register_2_q, register_3_q, register_4_q;

  Decoder #(.select(2)) decoder_1 (
    .out0(decoder_1_out0), .out1(decoder_1_out1), .out2(decoder_1_out2), .out3(decoder_1_out3), .sel(B),
    .en(C));
  Clock CLK (.out(CLK_out));
  Register register_1 (.D(A), .en(decoder_1_out0), .Q(register_1_q), .clk(CLK_out));  // open: clr
  Register register_2 (.D(A), .en(decoder_1_out1), .Q(register_2_q), .clk(CLK_out));  // open: clr
  Register register_3 (.D(A), .en(decoder_1_out2), .Q(register_3_q), .clk(CLK_out));  // open: clr
  Register register_4 (.D(A), .en(decoder_1_out3), .Q(register_4_q), .clk(CLK_out));  // open: clr
  Multiplexer #(.select(2), .width(8), .enable("false")) multiplexer_1 (
    .in0(register_1_q), .in1(register_2_q), .in2(register_3_q), .in3(register_4_q), .out(F), .sel(B));
endmodule
