// Logisim project register files_cai tien.circ as structural Verilog: 1 circuit, main circuit main
module main (
  input  [7:0] A,
  input  [1:0] C1,
  input  [1:0] C2,
  input  En,
  output [7:0] F
);

  wire CLK_out, decoder_1_out0, decoder_1_out1, decoder_1_out2, decoder_1_out3;
  wire [7:0] R1_q, R2_q, R3_q, R4_q;

  Decoder #(.select(2)) decoder_1 (
    .out0(decoder_1_out0), .out1(decoder_1_out1), .out2(decoder_1_out2), .out3(decoder_1_out3), .sel(C1),
    .en(En));
  Clock CLK (.out(CLK_out));
  Register R1 (.D(A), .en(decoder_1_out0), .Q(R1_q), .clk(CLK_out));  // open: clr
  Register R2 (.D(A), .en(decoder_1_out1), .Q(R2_q), .clk(CLK_out));  // open: clr
  Register R3 (.D(A), .en(decoder_1_out2), .Q(R3_q), .clk(CLK_out));  // open: clr
  Register R4 (.D(A), .en(decoder_1_out3), .Q(R4_q), .clk(CLK_out));  // open: clr
  Multiplexer #(.select(2), .width(8), .enable("false")) multiplexer_1 (
    .in0(R1_q), .in1(R2_q), .in2(R3_q), .in3(R4_q), .out(F), .sel(C2));
endmodule
